// Logisim project pipline.circ as structural Verilog: 24 circuits, main circuit memwb_reg
module main (
  input  [7:0] INTERRUPTIONS,
  input  CLK,
  input  RST
);

  wire alu_1_out_5, alu_1_out_6, alu_1_out_7, control_unit_bpu_write_en, control_unit_cu_cp0_w_en,
       control_unit_cu_exmem_flush, control_unit_cu_exmem_stall, control_unit_cu_idex_flush,
       control_unit_cu_idex_stall, control_unit_cu_ifid_flush, control_unit_cu_ifid_stall,
       control_unit_cu_pc_stall, control_unit_out_21, control_unit_out_24, cp0_1_cp0_intr,
       cpu_interface_1_mem_stall, decoder_id_jump, decoder_id_rt_addr_sel, decoder_id_rt_data_sel,
       decoder_out_2, decoder_out_3, decoder_out_4, decoder_out_6, decoder_out_7, decoder_out_10,
       decoder_out_14, decoder_out_16, decoder_out_17, decoder_out_18, decoder_out_19, decoder_out_21,
       decoder_out_22, EXMEM_cp0_w_en_2, EXMEM_exmem_branch, EXMEM_exmem_eret, EXMEM_exmem_lf,
       EXMEM_exmem_mem_r, EXMEM_exmem_nen_w, EXMEM_exmem_reg_w, EXMEM_exmem_zf, EXMEM_mem_nop,
       EXMEM_syscall_2, idex_reg_ex_jmp, idex_reg_ex_jr, idex_reg_idex_b_sel, idex_reg_idex_branch,
       idex_reg_idex_cp0_w_en, idex_reg_idex_eret, idex_reg_idex_mem_r, idex_reg_idex_mem_w,
       idex_reg_idex_movnz, idex_reg_idex_movz, idex_reg_idex_of_w_disen, idex_reg_idex_reg_w,
       idex_reg_idex_shamt_sel, idex_reg_idex_syscall, ifid_reg_id_nop, memwb_reg_1_memwb_cp0_w_en,
       memwb_reg_1_memwb_mem_r, memwb_reg_1_memwb_reg_w, not_1_out, or_1_out, reg_w_gen_1_out_7;
  wire [1:0] decoder_id_rd_addr_sel_1_0, decoder_in_imm_ext_1_0, decoder_out_11, forwarding_unit_1_a_sel_1_0,
       forwarding_unit_1_b_sel_31_0, idex_reg_idex_exres_sel, idex_reg_idex_shift_op_1_0;
  wire [2:0] control_unit_cu_pc_src_2_0, decoder_out_5, decoder_out_8, decoder_out_12, decoder_out_13,
       decoder_out_20, EXMEM_exmem_condition_2_0, EXMEM_exmem_load_sel_2_0, idex_reg_idex_conition_2_0,
       idex_reg_idex_load_sel_2_0, idex_reg_idex_store_sel_2_0;
  wire [3:0] EXMEM_mem_byte_w_en, EXMEM_reg_byte_w_en_3_0_2, idex_reg_idex_alu_op_3_0,
       load_b_w_e_gen_b_w_en_3_0, memwb_reg_1_reg_byte_w_en_3_0_2, store_b_w_e_gen_b_w_en_3_0;
  wire [4:0] control_unit_cu_exec_code_4_0, decoder_cp0_src_addr_3_0, decoder_out_9, decoder_out_15,
       EXMEM_exmem_cp0_dst_addr_4_0, EXMEM_exmem_rd_addr_4_0, idex_reg_idex_cp0_addr_4_0,
       idex_reg_idex_rd_addr_4_0, idex_reg_idex_rs_addr_4_0, idex_reg_idex_rt_addr_4_0,
       idex_reg_idex_shamt_4_0, ifid_reg_ifid_rd_addr_4_0, ifid_reg_ifid_rs_addr_4_0,
       ifid_reg_ifid_rt_addr_4_0, memwb_reg_1_memwb_cp0_dst_addr_4_0, memwb_reg_1_memwb_rd_addr_4_0,
       multiplexer_2_out, multiplexer_4_out, multiplexer_9_out;
  wire [15:0] ifid_reg_ifid_imm_15_0;
  wire [31:0] adder_1_out, adder_2_out, alu_1_out_4, barrel_shifter_1_shift_out_31_0,
       branch_predict_unit_1_predicted_pc_31_0, control_unit_cu_epc_321_0, control_unit_cu_vector_31_0,
       cp0_1_cp0_data_31_0, cp0_1_cp0_epc_31_0, cpu_interface_1_dc_data_out, cpu_interface_1_ic_data_out,
       EXMEM_exmem_alu_res_31_0, EXMEM_exmem_pc_4_31_0, EXMEM_exmem_pc_31_0, EXMEM_exmem_rt_data_31_0,
       EXMEM_exmem_target_31_0, final_target_1_final_target_31_0, forwarding_unit_1_input_a_31_0,
       forwarding_unit_1_input_b_31_0, GPR_rs_data_31_0, GPR_rt_data_31_0, idex_reg_idex_imm_ext_31_0,
       idex_reg_idex_op_a_31_0, idex_reg_idex_op_b_31_0, idex_reg_idex_pc_4_31_0, idex_reg_idex_pc_31_0,
       ifid_reg_ifid_instr_31_0, ifid_reg_ifid_jump_instr_31_0, ifid_reg_ifid_pc_4_31_0,
       ifid_reg_ifid_pc_31_0, load_shifter_out_4, memwb_reg_1_aligned_rt_data_31_0_2,
       memwb_reg_1_memwb_exdata_31_0, memwb_reg_1_memwb_memdata_31_0, multiplexer_1_out, multiplexer_3_out,
       multiplexer_5_out, multiplexer_6_out, multiplexer_7_out, multiplexer_8_out, multiplexer_10_out,
       multiplexer_11_out, multiplexer_12_out, PC_pc_out_31_0, store_shifter_real_rt_data_31_0, undriven,
       \位扩展单元_imm_ext_31_0 ;

  branch_predict_unit branch_predict_unit_1 (
    .current_pc_31_0(PC_pc_out_31_0), .tag_pc_31_0(EXMEM_exmem_pc_31_0),
    .predicted_pc_31_0(branch_predict_unit_1_predicted_pc_31_0),
    .next_pc_31_0(final_target_1_final_target_31_0), .bpu_write_en(control_unit_bpu_write_en), .in_5(CLK),
    .in_6(RST));
  Multiplexer #(.select(3), .width(32), .disabled(0), .enable("false")) multiplexer_1 (
    .in0(ifid_reg_ifid_jump_instr_31_0), .in1(GPR_rs_data_31_0), .in2(control_unit_cu_vector_31_0),
    .in3(cp0_1_cp0_epc_31_0), .in4(final_target_1_final_target_31_0),
    .in5(branch_predict_unit_1_predicted_pc_31_0), .out(multiplexer_1_out), .sel(control_unit_cu_pc_src_2_0));  // open: in6, in7
  pc PC (
    .stall(control_unit_cu_pc_stall), .clk(CLK), .reset(RST), .pc_out_31_0(PC_pc_out_31_0),
    .pc_in_31_0(multiplexer_1_out));
  cpu_interface cpu_interface_1 (
    .clk(CLK), .reset(RST), .ic_addr(PC_pc_out_31_0[29:0]), .dc_read_in(EXMEM_exmem_mem_r),
    .dc_write_in(EXMEM_exmem_nen_w), .dc_addr(EXMEM_exmem_alu_res_31_0[31:2]),
    .data_reg(EXMEM_exmem_rt_data_31_0), .dc_byte_w_en(EXMEM_mem_byte_w_en),
    .ic_data_out(cpu_interface_1_ic_data_out), .dc_data_out(cpu_interface_1_dc_data_out),
    .mem_stall(cpu_interface_1_mem_stall));
  ifid_reg ifid_reg (
    .clk(CLK), .reset(RST), .ifid_pc_31_0(ifid_reg_ifid_pc_31_0), .cu_stall(control_unit_cu_ifid_stall),
    .cu_flush(control_unit_cu_ifid_flush), .ifid_rs_addr_4_0(ifid_reg_ifid_rs_addr_4_0),
    .ifid_rt_addr_4_0(ifid_reg_ifid_rt_addr_4_0), .pc_31_0(PC_pc_out_31_0),
    .ifid_rd_addr_4_0(ifid_reg_ifid_rd_addr_4_0), .ifid_imm_15_0(ifid_reg_ifid_imm_15_0),
    .pc_4_31_0(adder_1_out), .ifid_pc_4_31_0(ifid_reg_ifid_pc_4_31_0),
    .instr_31_0(cpu_interface_1_ic_data_out), .ifid_jump_instr_31_0(ifid_reg_ifid_jump_instr_31_0),
    .ifid_instr_31_0(ifid_reg_ifid_instr_31_0), .id_nop(ifid_reg_id_nop));
  Adder #(.width(32)) adder_1 (.a(PC_pc_out_31_0), .b(32'h4), .out(adder_1_out));  // open: cin, cout
  decoder decoder (
    .cp0_src_addr_3_0(decoder_cp0_src_addr_3_0), .id_rt_data_sel(decoder_id_rt_data_sel),
    .id_rd_addr_sel_1_0(decoder_id_rd_addr_sel_1_0), .ifid_instr_31_0(ifid_reg_ifid_instr_31_0),
    .id_jump(decoder_id_jump), .in_imm_ext_1_0(decoder_in_imm_ext_1_0),
    .id_rt_addr_sel(decoder_id_rt_addr_sel), .out_2(decoder_out_2), .out_3(decoder_out_3),
    .out_4(decoder_out_4), .out_5(decoder_out_5), .out_6(decoder_out_6), .out_7(decoder_out_7),
    .out_9(decoder_out_9), .out_10(decoder_out_10), .out_11(decoder_out_11), .out_12(decoder_out_12),
    .out_13(decoder_out_13), .out_14(decoder_out_14), .out_15(decoder_out_15), .out_16(decoder_out_16),
    .out_17(decoder_out_17), .out_18(decoder_out_18), .out_20(decoder_out_20), .out_19(decoder_out_19),
    .out_21(decoder_out_21), .out_22(decoder_out_22), .out_8(decoder_out_8));
  GPR GPR (
    .clk(not_1_out), .reset(RST), .Rs_data_31_0(GPR_rs_data_31_0), .Rs_addr_4_0(ifid_reg_ifid_rs_addr_4_0),
    .Rt_addr_4_0(multiplexer_2_out), .Rd_addr_4_0(memwb_reg_1_memwb_rd_addr_4_0),
    .Rt_data_31_0(GPR_rt_data_31_0), .write(memwb_reg_1_memwb_reg_w), .data_in_31_0(multiplexer_12_out),
    .Rd_byte_w_en_3_0(memwb_reg_1_reg_byte_w_en_3_0_2));
  not not_1 (not_1_out, CLK);
  Multiplexer #(.width(5), .enable("false")) multiplexer_2 (
    .in0(ifid_reg_ifid_rt_addr_4_0), .in1({5{1'b0}}), .out(multiplexer_2_out), .sel(decoder_id_rt_addr_sel));
  Multiplexer #(.width(32), .enable("false")) multiplexer_3 (
    .in0(cp0_1_cp0_data_31_0), .in1(GPR_rt_data_31_0), .out(multiplexer_3_out), .sel(decoder_id_rt_data_sel));
  imm_ext \u_位扩展单元  (
    .ifid_imm_15_0(ifid_reg_ifid_imm_15_0), .imm_ext_31_0(\位扩展单元_imm_ext_31_0 ),
    .id_imm_ext_1_0(decoder_id_rd_addr_sel_1_0));
  Multiplexer #(.select(2), .width(5), .enable("false")) multiplexer_4 (
    .in0(ifid_reg_ifid_rt_addr_4_0), .in1(ifid_reg_ifid_rd_addr_4_0), .in2({5{1'b1}}),
    .out(multiplexer_4_out), .sel(decoder_in_imm_ext_1_0));  // open: in3
  control_unit control_unit (
    .id_jmp(decoder_id_jump), .cu_ifid_stall(control_unit_cu_ifid_stall),
    .cu_idex_flush(control_unit_cu_idex_flush), .cu_idex_stall(control_unit_cu_idex_stall),
    .preedicted_idex_pc_31_0(idex_reg_idex_pc_31_0), .cu_pc_stall(control_unit_cu_pc_stall),
    .cu_ifid_flush(control_unit_cu_ifid_flush), .mem_stall(cpu_interface_1_mem_stall),
    .target_exmem_pc_31_0(final_target_1_final_target_31_0), .exmem_syscall(EXMEM_syscall_2),
    .real_rs_addr_4_0(ifid_reg_ifid_rs_addr_4_0), .real_rd_addr_4_0(idex_reg_idex_rd_addr_4_0),
    .cu_exmem_stall(control_unit_cu_exmem_stall), .cu_exmem_flush(control_unit_cu_exmem_flush),
    .id_jr(EXMEM_mem_nop), .bpu_write_en(control_unit_bpu_write_en), .real_rt_addr_4_0(multiplexer_2_out),
    .cp0_intr(cp0_1_cp0_intr), .exmem_eret(EXMEM_exmem_eret), .cu_cp0_w_en(control_unit_cu_cp0_w_en),
    .cu_exec_code_4_0(control_unit_cu_exec_code_4_0), .cu_epc_321_0(control_unit_cu_epc_321_0),
    .cu_vector_31_0(control_unit_cu_vector_31_0), .cu_pc_src_2_0(control_unit_cu_pc_src_2_0),
    .idex_mem_r(idex_reg_idex_mem_r), .out_22(CLK), .out_23(RST), .out_21(control_unit_out_21),
    .out_24(control_unit_out_24));
  idex_reg idex_reg (
    .idex_mem_w(idex_reg_idex_mem_w), .idex_mem_r(idex_reg_idex_mem_r), .clk(CLK),
    .idex_reg_w(idex_reg_idex_reg_w), .reset(RST), .idex_branch(idex_reg_idex_branch),
    .cu_stall(control_unit_cu_idex_stall), .idex_conition_2_0(idex_reg_idex_conition_2_0),
    .cu_flush(control_unit_cu_idex_flush), .idex_of_w_disen(idex_reg_idex_of_w_disen),
    .id_rd_addr_4_0(multiplexer_4_out), .idex_exres_sel(idex_reg_idex_exres_sel),
    .idex_B_sel(idex_reg_idex_b_sel), .idex_ALU_op_3_0(idex_reg_idex_alu_op_3_0),
    .ifid_pc_31_0(ifid_reg_ifid_pc_31_0), .idex_shamt_sel(idex_reg_idex_shamt_sel),
    .idex_shift_op_1_0(idex_reg_idex_shift_op_1_0), .idex_shamt_4_0(idex_reg_idex_shamt_4_0),
    .ifid_pc_4_31_0(ifid_reg_ifid_pc_4_31_0), .idex_rs_addr_4_0(idex_reg_idex_rs_addr_4_0),
    .idex_rt_addr_4_0(idex_reg_idex_rt_addr_4_0), .idex_rd_addr_4_0(idex_reg_idex_rd_addr_4_0),
    .gpr_rs_31_0(GPR_rs_data_31_0), .idex_op_A_31_0(idex_reg_idex_op_a_31_0),
    .gpr_rt_31_0(multiplexer_3_out), .idex_op_B_31_0(idex_reg_idex_op_b_31_0),
    .id_imm_ext_31_0(\位扩展单元_imm_ext_31_0 ), .idex_imm_ext_31_0(idex_reg_idex_imm_ext_31_0),
    .idex_pc_31_0(idex_reg_idex_pc_31_0), .idex_pc_4_31_0(idex_reg_idex_pc_4_31_0),
    .idex_load_sel_2_0(idex_reg_idex_load_sel_2_0), .idex_store_sel_2_0(idex_reg_idex_store_sel_2_0),
    .idex_cp0_addr_4_0(idex_reg_idex_cp0_addr_4_0), .idex_syscall(idex_reg_idex_syscall),
    .idex_cp0_w_en(idex_reg_idex_cp0_w_en), .idex_eret(idex_reg_idex_eret), .idex_movz(idex_reg_idex_movz),
    .idex_movnz(idex_reg_idex_movnz), .in_13(decoder_out_2), .in_14(decoder_out_3), .in_15(decoder_out_4),
    .in_19(decoder_out_6), .in_23(decoder_out_5), .in_27(decoder_out_7), .in_16(decoder_out_8),
    .in_20(decoder_out_9), .in_24(decoder_out_10), .in_28(decoder_out_11), .in_31(decoder_out_12),
    .in_17(decoder_out_13), .in_21(decoder_out_14), .in_25(decoder_out_15), .in_29(decoder_out_16),
    .in_32(decoder_out_17), .in_18(decoder_out_18), .in_22(decoder_out_19), .in_26(decoder_out_20),
    .in_30(decoder_out_21), .in_33(decoder_out_22), .in_12(decoder_id_jump), .in_11(ifid_reg_id_nop),
    .ex_nop(control_unit_out_24), .ex_jmp(idex_reg_ex_jmp), .ex_jr(idex_reg_ex_jr));
  or or_1 (or_1_out, idex_reg_idex_movz, idex_reg_idex_movnz);
  forwarding_unit forwarding_unit_1 (
    .rs_data_31_0(idex_reg_idex_op_a_31_0), .rt_data_31_0(idex_reg_idex_op_b_31_0),
    .memwb_byte_en_3_0(memwb_reg_1_reg_byte_w_en_3_0_2), .rs_addr(idex_reg_idex_rs_addr_4_0),
    .rt_addr(idex_reg_idex_rt_addr_4_0), .memwb_rd_addr_4_0(memwb_reg_1_memwb_rd_addr_4_0),
    .input_A_31_0(forwarding_unit_1_input_a_31_0), .input_B_31_0(forwarding_unit_1_input_b_31_0),
    .A_sel_1_0(forwarding_unit_1_a_sel_1_0), .memwb_data_31_0(multiplexer_12_out),
    .B_sel_31_0(forwarding_unit_1_b_sel_31_0), .exmem_rd_addr(EXMEM_exmem_rd_addr_4_0),
    .exmem_byte_en_3_0(EXMEM_reg_byte_w_en_3_0_2));
  Multiplexer #(.select(2), .width(32), .enable("false")) multiplexer_5 (
    .in0(idex_reg_idex_op_a_31_0), .in1(EXMEM_exmem_alu_res_31_0), .in2(forwarding_unit_1_input_a_31_0),
    .out(multiplexer_5_out), .sel(forwarding_unit_1_a_sel_1_0));  // open: in3
  Multiplexer #(.select(2), .width(32), .enable("false")) multiplexer_6 (
    .in0(idex_reg_idex_op_b_31_0), .in1(EXMEM_exmem_alu_res_31_0), .in2(forwarding_unit_1_input_b_31_0),
    .out(multiplexer_6_out), .sel(forwarding_unit_1_b_sel_31_0));  // open: in3
  Multiplexer #(.width(32), .enable("false")) multiplexer_7 (
    .in0(multiplexer_5_out), .in1(undriven), .out(multiplexer_7_out), .sel(or_1_out));
  Multiplexer #(.width(32), .enable("false")) multiplexer_8 (
    .in0(multiplexer_6_out), .in1(idex_reg_idex_imm_ext_31_0), .out(multiplexer_8_out),
    .sel(idex_reg_idex_b_sel));
  Multiplexer #(.width(5), .enable("false")) multiplexer_9 (
    .in0(idex_reg_idex_shamt_4_0), .in1(multiplexer_5_out[4:0]), .out(multiplexer_9_out),
    .sel(idex_reg_idex_shamt_sel));
  ALU alu_1 (
    .in_2(multiplexer_7_out), .in_3(multiplexer_8_out), .in_1(idex_reg_idex_alu_op_3_0), .out_4(alu_1_out_4),
    .out_5(alu_1_out_5), .out_6(alu_1_out_6), .out_7(alu_1_out_7));
  barrel_shifter barrel_shifter_1 (
    .shift_amount_4_0(multiplexer_9_out), .shift_op_1_0(idex_reg_idex_shift_op_1_0),
    .shift_in_31_0(multiplexer_6_out), .shift_out_31_0(barrel_shifter_1_shift_out_31_0));
  reg_w_gen reg_w_gen_1 (
    .in_3(idex_reg_idex_movz), .in_4(idex_reg_idex_movnz), .in_5(idex_reg_idex_reg_w),
    .in_6(idex_reg_idex_of_w_disen), .out_7(reg_w_gen_1_out_7), .in_1(alu_1_out_7), .in_2(alu_1_out_6));
  Adder #(.width(32)) adder_2 (
    .a({idex_reg_idex_imm_ext_31_0[29:0], 2'b00}), .b(idex_reg_idex_pc_4_31_0), .out(adder_2_out));  // open: cin, cout
  Multiplexer #(.width(32), .disabled(0), .enable("false")) multiplexer_10 (
    .in0(adder_2_out), .in1(alu_1_out_4), .out(multiplexer_10_out), .sel(idex_reg_ex_jr));
  lw_b_w_e_gen load_b_w_e_gen (
    .addr_1_0(alu_1_out_4[1:0]), .load_sel_2_0(idex_reg_idex_load_sel_2_0),
    .b_w_en_3_0(load_b_w_e_gen_b_w_en_3_0));
  sw_b_w_e_gen store_b_w_e_gen (
    .addr_1_0(alu_1_out_4[1:0]), .store_sel_2_0(idex_reg_idex_store_sel_2_0),
    .b_w_en_3_0(store_b_w_e_gen_b_w_en_3_0));
  real_rt_data_gen store_shifter (
    .addr_1_0(alu_1_out_4[1:0]), .store_sel_2_0(idex_reg_idex_store_sel_2_0),
    .rt_data_31_0(multiplexer_6_out), .real_rt_data_31_0(store_shifter_real_rt_data_31_0));
  Multiplexer #(.select(2), .width(32), .enable("false")) multiplexer_11 (
    .in0(alu_1_out_4), .in1(barrel_shifter_1_shift_out_31_0), .in2(multiplexer_10_out),
    .in3(multiplexer_5_out), .out(multiplexer_11_out), .sel(idex_reg_idex_exres_sel));
  exmem_reg EXMEM (
    .clk(CLK), .idex_branch(idex_reg_idex_branch), .reset(RST),
    .idex_condition_2_0(idex_reg_idex_conition_2_0), .cu_stall(control_unit_cu_exmem_stall),
    .cu_flush(control_unit_cu_exmem_flush), .adder_target_31_0(multiplexer_10_out),
    .idex_mem_w(idex_reg_idex_mem_w), .idex_pc_31_0(idex_reg_idex_pc_31_0), .idex_memr(idex_reg_idex_mem_r),
    .idex_pc_4_31_0(idex_reg_idex_pc_4_31_0), .alu_lf(alu_1_out_5), .alu_zf(alu_1_out_6),
    .aligned_rt_data_31_0(store_shifter_real_rt_data_31_0), .ex_res_31_0(multiplexer_11_out),
    .real_rd_addr_4_0(idex_reg_idex_rd_addr_4_0), .idex_load_sel_2_0(idex_reg_idex_load_sel_2_0),
    .exmem_nen_w(EXMEM_exmem_nen_w), .exmem_mem_r(EXMEM_exmem_mem_r), .exmem_reg_w(EXMEM_exmem_reg_w),
    .exmem_condition_2_0(EXMEM_exmem_condition_2_0), .exmem_branch(EXMEM_exmem_branch),
    .exmem_alu_res_31_0(EXMEM_exmem_alu_res_31_0), .exmem_rt_data_31_0(EXMEM_exmem_rt_data_31_0),
    .exmem_target_31_0(EXMEM_exmem_target_31_0), .exmem_lf(EXMEM_exmem_lf), .exmem_zf(EXMEM_exmem_zf),
    .exmem_pc_31_0(EXMEM_exmem_pc_31_0), .exmem_pc_4_31_0(EXMEM_exmem_pc_4_31_0),
    .exmem_rd_addr_4_0(EXMEM_exmem_rd_addr_4_0), .exmem_load_sel_2_0(EXMEM_exmem_load_sel_2_0),
    .reg_byte_w_en_3_0(load_b_w_e_gen_b_w_en_3_0), .mem_byte_w_en_3_0(store_b_w_e_gen_b_w_en_3_0),
    .reg_byte_w_en_3_0_2(EXMEM_reg_byte_w_en_3_0_2), .mem_byte_w_en(EXMEM_mem_byte_w_en),
    .idex_cp0_dst_addr_4_0(idex_reg_idex_cp0_addr_4_0), .cp0_w_en(idex_reg_idex_cp0_w_en),
    .syscall(idex_reg_idex_syscall), .exmem_cp0_dst_addr_4_0(EXMEM_exmem_cp0_dst_addr_4_0),
    .cp0_w_en_2(EXMEM_cp0_w_en_2), .syscall_2(EXMEM_syscall_2), .idex_eret(idex_reg_idex_eret),
    .exmem_eret(EXMEM_exmem_eret), .alu_of(alu_1_out_7), .idex_reg_w(reg_w_gen_1_out_7),
    .ex_nop(control_unit_out_24), .ex_jmp(idex_reg_ex_jmp), .mem_nop(EXMEM_mem_nop),
    .mem_jmp(control_unit_out_21));  // open: exmem_store_sel_2_0
  cp0 cp0_1 (
    .cu_cp0_w_en(control_unit_cu_cp0_w_en), .cu_exec_code_4_0(control_unit_cu_exec_code_4_0),
    .wb_cp0_w_en(memwb_reg_1_memwb_cp0_w_en), .wb_cp0_data_in_31_0(memwb_reg_1_aligned_rt_data_31_0_2),
    .eoc_31_0(control_unit_cu_epc_321_0), .cp0_data_31_0(cp0_1_cp0_data_31_0), .cp0_intr(cp0_1_cp0_intr),
    .cp0_epc_31_0(cp0_1_cp0_epc_31_0), .interruption_7_0(INTERRUPTIONS),
    .id_cp0_src_addr_4_0(decoder_cp0_src_addr_3_0), .wb_cp0_dst_addr_4_0(memwb_reg_1_memwb_cp0_dst_addr_4_0));
  final_target final_target_1 (
    .exmem_branch(EXMEM_exmem_branch), .exmem_condition_2_0(EXMEM_exmem_condition_2_0),
    .exmem_lf(EXMEM_exmem_lf), .exmem_zf(EXMEM_exmem_zf), .exmem_target_31_0(EXMEM_exmem_target_31_0),
    .exmem_pc_4_31_0(EXMEM_exmem_pc_4_31_0), .final_target_31_0(final_target_1_final_target_31_0));
  mem_r_data_shift load_shifter (
    .in_1(EXMEM_exmem_alu_res_31_0[1:0]), .in_2(EXMEM_exmem_load_sel_2_0),
    .in_3(cpu_interface_1_dc_data_out), .out_4(load_shifter_out_4));
  memwb_reg memwb_reg_1 (
    .clk(CLK), .reset(RST), .exmem_mem_r(EXMEM_exmem_mem_r), .exmem_mem_w(EXMEM_exmem_reg_w),
    .exmem_rd_addr_4_0(EXMEM_exmem_rd_addr_4_0), .reg_byte_w_en_3_0(EXMEM_reg_byte_w_en_3_0_2),
    .mem_data_31_0(load_shifter_out_4), .ex_data_31_0(EXMEM_exmem_alu_res_31_0),
    .memwb_mem_r(memwb_reg_1_memwb_mem_r), .memwb_reg_w(memwb_reg_1_memwb_reg_w),
    .memwb_rd_addr_4_0(memwb_reg_1_memwb_rd_addr_4_0), .reg_byte_w_en_3_0_2(memwb_reg_1_reg_byte_w_en_3_0_2),
    .memwb_memdata_31_0(memwb_reg_1_memwb_memdata_31_0), .memwb_exdata_31_0(memwb_reg_1_memwb_exdata_31_0),
    .exmem_cp0_dst_addr_4_0(EXMEM_exmem_cp0_dst_addr_4_0), .exmem_cp0_w_en(EXMEM_cp0_w_en_2),
    .memwb_cp0_dst_addr_4_0(memwb_reg_1_memwb_cp0_dst_addr_4_0), .memwb_cp0_w_en(memwb_reg_1_memwb_cp0_w_en),
    .aligned_rt_data_31_0(EXMEM_exmem_rt_data_31_0),
    .aligned_rt_data_31_0_2(memwb_reg_1_aligned_rt_data_31_0_2));
  Multiplexer #(.width(32), .enable("false")) multiplexer_12 (
    .in0(memwb_reg_1_memwb_memdata_31_0), .in1(memwb_reg_1_memwb_exdata_31_0), .out(multiplexer_12_out),
    .sel(memwb_reg_1_memwb_mem_r));

  // Notes on the sheet:
  //   byte_en
  //   addr
  //   write
  //   data
  //   JR使用的从Rs读出的数据
  //   Rd_addr_sel
  //   new_reg_w = ((movnz && zf) || (movz && !zf) || (id_of_w_disen && of)) ? 0 : idex_reg_w
  //   32'd0
  //   Rt_imm_sel
  //   shift_amount_sel
  //   ALU
  //   Barrel Shifter
  //   Exec_res_sel
endmodule

module ifid_reg (
  input  clk,
  input  reset,
  input  cu_stall,
  input  cu_flush,
  input  [31:0] pc_31_0,
  input  [31:0] pc_4_31_0,
  input  [31:0] instr_31_0,
  output [31:0] ifid_pc_31_0,
  output [31:0] ifid_pc_4_31_0,
  output [31:0] ifid_jump_instr_31_0,
  output [31:0] ifid_instr_31_0,
  output [4:0] ifid_rs_addr_4_0,
  output [4:0] ifid_rt_addr_4_0,
  output [15:0] ifid_imm_15_0,
  output [4:0] ifid_rd_addr_4_0,
  output id_nop
);
endmodule

module decoder (
  input  [31:0] ifid_instr_31_0,
  output out_2,
  output out_3,
  output out_4,
  output [2:0] out_5,
  output out_6,
  output out_7,
  output [2:0] out_8,
  output [4:0] out_9,
  output out_10,
  output [1:0] out_11,
  output [2:0] out_12,
  output [2:0] out_13,
  output out_14,
  output [4:0] out_15,
  output out_16,
  output out_17,
  output out_18,
  output out_19,
  output [2:0] out_20,
  output out_21,
  output out_22,
  output [4:0] cp0_src_addr_3_0,
  output id_rt_data_sel,
  output [1:0] id_rd_addr_sel_1_0,
  output id_jump,
  output [1:0] in_imm_ext_1_0,
  output id_rt_addr_sel
);
endmodule

module idex_reg (
  input  clk,
  input  reset,
  input  cu_stall,
  input  cu_flush,
  input  [4:0] id_rd_addr_4_0,
  input  [31:0] ifid_pc_31_0,
  input  [31:0] ifid_pc_4_31_0,
  input  [31:0] gpr_rs_31_0,
  input  [31:0] gpr_rt_31_0,
  input  [31:0] id_imm_ext_31_0,
  input  in_11,
  input  in_12,
  input  in_13,
  input  in_14,
  input  in_15,
  input  [2:0] in_16,
  input  [2:0] in_17,
  input  in_18,
  input  in_19,
  input  [4:0] in_20,
  input  in_21,
  input  in_22,
  input  [2:0] in_23,
  input  in_24,
  input  [4:0] in_25,
  input  [2:0] in_26,
  input  in_27,
  input  [1:0] in_28,
  input  in_29,
  input  in_30,
  input  [2:0] in_31,
  input  in_32,
  input  in_33,
  output idex_movz,
  output idex_movnz,
  output idex_mem_w,
  output idex_mem_r,
  output idex_reg_w,
  output idex_branch,
  output [2:0] idex_conition_2_0,
  output idex_of_w_disen,
  output [1:0] idex_exres_sel,
  output idex_B_sel,
  output [3:0] idex_ALU_op_3_0,
  output idex_shamt_sel,
  output [4:0] idex_shamt_4_0,
  output [1:0] idex_shift_op_1_0,
  output [31:0] idex_imm_ext_31_0,
  output [4:0] idex_rd_addr_4_0,
  output [31:0] idex_pc_31_0,
  output [31:0] idex_pc_4_31_0,
  output [2:0] idex_load_sel_2_0,
  output [2:0] idex_store_sel_2_0,
  output [31:0] idex_op_A_31_0,
  output [31:0] idex_op_B_31_0,
  output [4:0] idex_rs_addr_4_0,
  output [4:0] idex_rt_addr_4_0,
  output [4:0] idex_cp0_addr_4_0,
  output idex_cp0_w_en,
  output idex_syscall,
  output idex_eret,
  output ex_nop,
  output ex_jmp,
  output ex_jr
);


  assign idex_movnz = 1'b1;
  assign idex_movz = 1'b1;
endmodule

module exmem_reg (
  input  clk,
  input  reset,
  input  cu_stall,
  input  cu_flush,
  input  idex_mem_w,
  input  idex_memr,
  input  idex_reg_w,
  input  idex_branch,
  input  [2:0] idex_condition_2_0,
  input  [31:0] adder_target_31_0,
  input  alu_lf,
  input  alu_zf,
  input  alu_of,
  input  [31:0] ex_res_31_0,
  input  [4:0] real_rd_addr_4_0,
  input  [2:0] idex_load_sel_2_0,
  input  [3:0] reg_byte_w_en_3_0,
  input  [3:0] mem_byte_w_en_3_0,
  input  [31:0] idex_pc_31_0,
  input  [31:0] idex_pc_4_31_0,
  input  [31:0] aligned_rt_data_31_0,
  input  [4:0] idex_cp0_dst_addr_4_0,
  input  cp0_w_en,
  input  syscall,
  input  idex_eret,
  input  ex_nop,
  input  ex_jmp,
  output [31:0] exmem_pc_31_0,
  output exmem_nen_w,
  output exmem_mem_r,
  output exmem_reg_w,
  output [3:0] reg_byte_w_en_3_0_2,
  output [4:0] exmem_rd_addr_4_0,
  output [3:0] mem_byte_w_en,
  output [31:0] exmem_alu_res_31_0,
  output [31:0] exmem_rt_data_31_0,
  output exmem_branch,
  output [2:0] exmem_condition_2_0,
  output [31:0] exmem_target_31_0,
  output [31:0] exmem_pc_4_31_0,
  output exmem_lf,
  output exmem_zf,
  output [2:0] exmem_load_sel_2_0,
  output [2:0] exmem_store_sel_2_0,
  output [4:0] exmem_cp0_dst_addr_4_0,
  output cp0_w_en_2,
  output syscall_2,
  output exmem_eret,
  output mem_nop,
  output mem_jmp
);
endmodule

module memwb_reg (
  input  clk,
  input  reset,
  input  exmem_mem_r,
  input  exmem_mem_w,
  input  [3:0] reg_byte_w_en_3_0,
  input  [4:0] exmem_rd_addr_4_0,
  input  [31:0] mem_data_31_0,
  input  [31:0] ex_data_31_0,
  input  [4:0] exmem_cp0_dst_addr_4_0,
  input  exmem_cp0_w_en,
  input  [31:0] aligned_rt_data_31_0,
  output memwb_mem_r,
  output memwb_reg_w,
  output [4:0] memwb_rd_addr_4_0,
  output [3:0] reg_byte_w_en_3_0_2,
  output [31:0] memwb_memdata_31_0,
  output [31:0] memwb_exdata_31_0,
  output [4:0] memwb_cp0_dst_addr_4_0,
  output memwb_cp0_w_en,
  output [31:0] aligned_rt_data_31_0_2
);
endmodule

module ALU (
  input  [3:0] in_1,
  input  [31:0] in_2,
  input  [31:0] in_3,
  output [31:0] out_4,
  output out_5,
  output out_6,
  output out_7
);
endmodule

module lw_b_w_e_gen (
  input  [1:0] addr_1_0,
  input  [2:0] load_sel_2_0,
  output [3:0] b_w_en_3_0
);
endmodule

module sw_b_w_e_gen (
  input  [1:0] addr_1_0,
  input  [2:0] store_sel_2_0,
  output [3:0] b_w_en_3_0
);
endmodule

module real_rt_data_gen (
  input  [1:0] addr_1_0,
  input  [2:0] store_sel_2_0,
  input  [31:0] rt_data_31_0,
  output [31:0] real_rt_data_31_0
);
endmodule

module barrel_shifter (
  input  [4:0] shift_amount_4_0,
  input  [1:0] shift_op_1_0,
  input  [31:0] shift_in_31_0,
  output [31:0] shift_out_31_0
);
endmodule

module GPR (
  input  clk,
  input  reset,
  input  [4:0] Rs_addr_4_0,
  input  [4:0] Rt_addr_4_0,
  input  [31:0] data_in_31_0,
  input  write,
  input  [4:0] Rd_addr_4_0,
  input  [3:0] Rd_byte_w_en_3_0,
  output [31:0] Rs_data_31_0,
  output [31:0] Rt_data_31_0
);
endmodule

module mem_r_data_shift (
  input  [1:0] in_1,
  input  [2:0] in_2,
  input  [31:0] in_3,
  output [31:0] out_4
);
endmodule

module final_target (
  input  exmem_branch,
  input  [2:0] exmem_condition_2_0,
  input  [31:0] exmem_target_31_0,
  input  [31:0] exmem_pc_4_31_0,
  input  exmem_lf,
  input  exmem_zf,
  output [31:0] final_target_31_0
);
endmodule

module pc (
  input  stall,
  input  clk,
  input  reset,
  input  [31:0] pc_in_31_0,
  output [31:0] pc_out_31_0
);
endmodule

module imm_ext (
  input  [15:0] ifid_imm_15_0,
  input  [1:0] id_imm_ext_1_0,
  output [31:0] imm_ext_31_0
);
endmodule

module control_unit (
  input  id_jr,
  input  mem_stall,
  input  id_jmp,
  input  exmem_syscall,
  input  idex_mem_r,
  input  [4:0] real_rs_addr_4_0,
  input  [4:0] real_rt_addr_4_0,
  input  [4:0] real_rd_addr_4_0,
  input  [31:0] preedicted_idex_pc_31_0,
  input  [31:0] target_exmem_pc_31_0,
  input  cp0_intr,
  input  exmem_eret,
  output [2:0] cu_pc_src_2_0,
  output cu_pc_stall,
  output cu_ifid_stall,
  output cu_ifid_flush,
  output cu_idex_stall,
  output cu_idex_flush,
  output cu_exmem_stall,
  output cu_exmem_flush,
  output out_21,
  output out_22,
  output out_23,
  output out_24,
  output bpu_write_en,
  output cu_cp0_w_en,
  output [4:0] cu_exec_code_4_0,
  output [31:0] cu_epc_321_0,
  output [31:0] cu_vector_31_0
);
endmodule

module forwarding_unit (
  input  [31:0] rs_data_31_0,
  input  [31:0] rt_data_31_0,
  input  [4:0] rs_addr,
  input  [4:0] rt_addr,
  input  [3:0] exmem_byte_en_3_0,
  input  [4:0] exmem_rd_addr,
  input  [3:0] memwb_byte_en_3_0,
  input  [4:0] memwb_rd_addr_4_0,
  input  [31:0] memwb_data_31_0,
  output [31:0] input_A_31_0,
  output [31:0] input_B_31_0,
  output [1:0] A_sel_1_0,
  output [1:0] B_sel_31_0
);
endmodule

module branch_predict_unit (
  input  [31:0] current_pc_31_0,
  input  [31:0] tag_pc_31_0,
  input  [31:0] next_pc_31_0,
  input  bpu_write_en,
  input  in_5,
  input  in_6,
  output [31:0] predicted_pc_31_0
);
endmodule

module cp0 (
  input  cu_cp0_w_en,
  input  [4:0] cu_exec_code_4_0,
  input  [7:0] interruption_7_0,
  input  [4:0] id_cp0_src_addr_4_0,
  input  wb_cp0_w_en,
  input  [4:0] wb_cp0_dst_addr_4_0,
  input  [31:0] wb_cp0_data_in_31_0,
  input  [31:0] eoc_31_0,
  output [31:0] cp0_data_31_0,
  output cp0_intr,
  output [31:0] cp0_epc_31_0
);
endmodule

module exception (
  input  in_1,
  input  [31:0] in_2,
  output out_3,
  output [4:0] out_4
);
endmodule

module pc_src_selector (
  input  [2:0] PC_SRC_2_0,
  input  [31:0] J_31_0,
  input  [31:0] JR_31_0,
  input  [31:0] VECTOR_31_0,
  input  [31:0] EPC_31_0,
  input  [31:0] TARGET_31_0,
  input  [31:0] BPU_31_0,
  output [31:0] PC_31_0
);
endmodule

module reg_w_gen (
  input  in_1,
  input  in_2,
  input  in_3,
  input  in_4,
  input  in_5,
  input  in_6,
  output out_7
);
endmodule

module cpu_interface (
  input  clk,
  input  reset,
  input  [29:0] ic_addr,
  input  dc_read_in,
  input  dc_write_in,
  input  [29:0] dc_addr,
  input  [31:0] data_reg,
  input  [3:0] dc_byte_w_en,
  output [31:0] ic_data_out,
  output [31:0] dc_data_out,
  output mem_stall
);
endmodule
