// Logisim project pipline_0.1.10.circ as structural Verilog: 29 circuits, main circuit main
module main (
  input  [7:0] INTERRUPTIONS,
  input  CLK,
  input  RST
);

  wire alu_1_out_5, alu_1_out_6, alu_1_out_7, control_unit_bpu_write_en, control_unit_cu_cp0_w_en,
       control_unit_cu_exmem_flush, control_unit_cu_exmem_stall, control_unit_cu_idex_flush,
       control_unit_cu_idex_stall, control_unit_cu_ifid_flush, control_unit_cu_ifid_stall,
       control_unit_cu_pc_stall, cp0_1_cp0_intr, decoder_id_ctrl, decoder_id_in, decoder_id_jump,
       decoder_id_rt_addr_sel, decoder_id_rt_data_sel, EXMEM_cp0_w_en_2, EXMEM_exmem_branch,
       EXMEM_exmem_eret, EXMEM_exmem_lf, EXMEM_exmem_mem_r, EXMEM_exmem_nen_w, EXMEM_exmem_reg_w,
       EXMEM_exmem_zf, EXMEM_syscall_2, idex_reg_idex_b_sel, idex_reg_idex_branch, idex_reg_idex_cp0_w_en,
       idex_reg_idex_eret, idex_reg_idex_mem_r, idex_reg_idex_mem_w, idex_reg_idex_movnz, idex_reg_idex_movz,
       idex_reg_idex_of_w_disen, idex_reg_idex_reg_w, idex_reg_idex_shamt_sel, idex_reg_idex_syscall,
       instr_mem_interface_men_stall, memwb_reg_1_memwb_cp0_w_en, memwb_reg_1_memwb_mem_r,
       memwb_reg_1_memwb_reg_w, or_1_out, reg_w_gen_1_out_7;
  wire [1:0] decoder_id_rd_addr_sel_1_0, decoder_in_imm_ext_1_0, forwarding_unit_1_a_sel_1_0,
       forwarding_unit_1_b_sel_31_0, idex_reg_idex_exres_sel, idex_reg_idex_shift_op_1_0, n32_2_1_out_2,
       n32_2_2_out_2;
  wire [2:0] control_unit_cu_pc_src_2_0, EXMEM_exmem_condition_2_0, EXMEM_exmem_load_sel_2_0,
       idex_reg_idex_conition_2_0, idex_reg_idex_load_sel_2_0, idex_reg_idex_store_sel_2_0;
  wire [3:0] EXMEM_mem_byte_w_en, EXMEM_reg_byte_w_en_3_0_2, idex_reg_idex_alu_op_3_0,
       load_b_w_e_gen_b_w_en_3_0, memwb_reg_1_reg_byte_w_en_3_0_2, store_b_w_e_gen_b_w_en_3_0;
  wire [4:0] control_unit_cu_exec_code_4_0, decoder_cp0_src_addr_3_0, EXMEM_exmem_cp0_dst_addr_4_0,
       EXMEM_exmem_rd_addr_4_0, idex_reg_idex_cp0_addr_4_0, idex_reg_idex_rd_addr_4_0,
       idex_reg_idex_rs_addr_4_0, idex_reg_idex_rt_addr_4_0, idex_reg_idex_shamt_4_0,
       ifid_reg_ifid_rd_addr_4_0, ifid_reg_ifid_rs_addr_4_0, ifid_reg_ifid_rt_addr_4_0,
       memwb_reg_1_memwb_cp0_dst_addr_4_0, memwb_reg_1_memwb_rd_addr_4_0, multiplexer_1_out,
       multiplexer_3_out, multiplexer_8_out, n32_5_1_out_2, undriven_2, undriven_3;
  wire [15:0] ifid_reg_ifid_imm_15_0;
  wire [31:0] adder_1_out, adder_2_out, alu_1_out_4, barrel_shifter_1_shift_out_31_0,
       branch_predict_unit_1_predicted_pc_31_0, control_unit_cu_epc_321_0, control_unit_cu_vector_31_0,
       cp0_1_cp0_data_31_0, cp0_1_cp0_epc_31_0, data_mem_interface_data_out_31_0, EXMEM_exmem_alu_res_31_0,
       EXMEM_exmem_pc_4_31_0, EXMEM_exmem_pc_31_0, EXMEM_exmem_rt_data_31_0, EXMEM_exmem_target_31_0,
       final_target_1_final_target_31_0, forwarding_unit_1_input_a_31_0, forwarding_unit_1_input_b_31_0,
       GPR_rs_data_31_0, GPR_rt_data_31_0, idex_reg_idex_imm_ext_31_0, idex_reg_idex_op_a_31_0,
       idex_reg_idex_op_b_31_0, idex_reg_idex_pc_4_31_0, idex_reg_idex_pc_31_0, ifid_reg_ifid_instr_31_0,
       ifid_reg_ifid_jump_instr_31_0, ifid_reg_ifid_pc_4_31_0, ifid_reg_ifid_pc_31_0,
       instr_mem_interface_instr_31_0, load_shifter_out_4, memwb_reg_1_aligned_rt_data_31_0_2,
       memwb_reg_1_memwb_exdata_31_0, memwb_reg_1_memwb_memdata_31_0, multiplexer_2_out, multiplexer_4_out,
       multiplexer_5_out, multiplexer_6_out, multiplexer_7_out, multiplexer_9_out, multiplexer_10_out,
       PC_pc_out_31_0, pc_src_selector_1_pc_31_0, store_shifter_real_rt_data_31_0, undriven, undriven_4,
       \位扩展单元_imm_ext_31_0 ;

  branch_predict_unit branch_predict_unit_1 (
    .current_pc_31_0(PC_pc_out_31_0), .tag_pc_31_0(EXMEM_exmem_pc_31_0),
    .predicted_pc_31_0(branch_predict_unit_1_predicted_pc_31_0),
    .next_pc_31_0(final_target_1_final_target_31_0), .bpu_write_en(control_unit_bpu_write_en));
  pc PC (
    .stall(control_unit_cu_pc_stall), .clk(CLK), .reset(RST), .pc_out_31_0(PC_pc_out_31_0),
    .pc_in_31_0(pc_src_selector_1_pc_31_0));
  pc_src_selector pc_src_selector_1 (
    .PC_SRC_2_0(control_unit_cu_pc_src_2_0), .J_31_0(ifid_reg_ifid_jump_instr_31_0),
    .JR_31_0(GPR_rs_data_31_0), .VECTOR_31_0(control_unit_cu_vector_31_0), .EPC_31_0(cp0_1_cp0_epc_31_0),
    .PC_31_0(pc_src_selector_1_pc_31_0), .TARGET_31_0(final_target_1_final_target_31_0),
    .BPU_31_0(branch_predict_unit_1_predicted_pc_31_0));
  instr_mem_interface instr_mem_interface (
    .clk(CLK), .cache_flush(RST), .instr_31_0(instr_mem_interface_instr_31_0), .addr_31_0(PC_pc_out_31_0),
    .men_stall(instr_mem_interface_men_stall));
  Adder #(.width(32)) adder_1 (.a(undriven), .b(PC_pc_out_31_0), .out(adder_1_out));  // open: cin, cout
  ifid_reg ifid_reg (
    .clk(CLK), .reset(RST), .ifid_pc_31_0(ifid_reg_ifid_pc_31_0), .cu_stall(control_unit_cu_ifid_stall),
    .cu_flush(control_unit_cu_ifid_flush), .ifid_rs_addr_4_0(ifid_reg_ifid_rs_addr_4_0),
    .ifid_rt_addr_4_0(ifid_reg_ifid_rt_addr_4_0), .pc_31_0(PC_pc_out_31_0),
    .ifid_rd_addr_4_0(ifid_reg_ifid_rd_addr_4_0), .ifid_imm_15_0(ifid_reg_ifid_imm_15_0),
    .pc_4_31_0(adder_1_out), .ifid_pc_4_31_0(ifid_reg_ifid_pc_4_31_0),
    .instr_31_0(instr_mem_interface_instr_31_0), .ifid_jump_instr_31_0(ifid_reg_ifid_jump_instr_31_0),
    .ifid_instr_31_0(ifid_reg_ifid_instr_31_0));
  decoder decoder (
    .cp0_src_addr_3_0(decoder_cp0_src_addr_3_0), .id_rt_data_sel(decoder_id_rt_data_sel),
    .id_rd_addr_sel_1_0(decoder_id_rd_addr_sel_1_0), .ifid_instr_31_0(ifid_reg_ifid_instr_31_0),
    .id_in(decoder_id_in), .id_jump(decoder_id_jump), .id_ctrl(decoder_id_ctrl),
    .in_imm_ext_1_0(decoder_in_imm_ext_1_0), .id_rt_addr_sel(decoder_id_rt_addr_sel));
  Multiplexer #(.width(5), .enable("false")) multiplexer_1 (
    .in0(ifid_reg_ifid_rt_addr_4_0), .in1(undriven_2), .out(multiplexer_1_out), .sel(decoder_id_rt_addr_sel));
  GPR GPR (
    .clk(CLK), .reset(RST), .Rs_data_31_0(GPR_rs_data_31_0), .Rs_addr_4_0(ifid_reg_ifid_rs_addr_4_0),
    .Rt_addr_4_0(multiplexer_1_out), .Rd_addr_4_0(memwb_reg_1_memwb_rd_addr_4_0),
    .Rt_data_31_0(GPR_rt_data_31_0), .write(memwb_reg_1_memwb_reg_w), .data_in_31_0(multiplexer_10_out),
    .Rd_byte_w_en_3_0(memwb_reg_1_reg_byte_w_en_3_0_2));
  imm_ext \u_位扩展单元  (
    .ifid_imm_15_0(ifid_reg_ifid_imm_15_0), .imm_ext_31_0(\位扩展单元_imm_ext_31_0 ),
    .id_imm_ext_1_0(decoder_in_imm_ext_1_0));
  Multiplexer #(.width(32), .enable("false")) multiplexer_2 (
    .in0(cp0_1_cp0_data_31_0), .in1(GPR_rt_data_31_0), .out(multiplexer_2_out), .sel(decoder_id_rt_data_sel));
  control_unit control_unit (
    .id_jmp(decoder_id_jump), .cu_idex_flush(control_unit_cu_idex_flush),
    .preedicted_idex_pc_31_0(idex_reg_idex_pc_31_0), .mem_stall(instr_mem_interface_men_stall),
    .exmem_syscall(EXMEM_syscall_2), .target_exmem_pc_31_0(final_target_1_final_target_31_0),
    .cu_ifid_flush(control_unit_cu_ifid_flush), .cu_idex_stall(control_unit_cu_idex_stall),
    .cu_ifid_stall(control_unit_cu_ifid_stall), .cu_pc_stall(control_unit_cu_pc_stall),
    .real_rs_addr_4_0(ifid_reg_ifid_rs_addr_4_0), .real_rd_addr_4_0(idex_reg_idex_rd_addr_4_0),
    .cu_exmem_stall(control_unit_cu_exmem_stall), .cu_exmem_flush(control_unit_cu_exmem_flush),
    .id_jr(decoder_id_in), .bpu_write_en(control_unit_bpu_write_en), .real_rt_addr_4_0(multiplexer_1_out),
    .cp0_intr(cp0_1_cp0_intr), .exmem_eret(EXMEM_exmem_eret), .cu_cp0_w_en(control_unit_cu_cp0_w_en),
    .cu_exec_code_4_0(control_unit_cu_exec_code_4_0), .cu_epc_321_0(control_unit_cu_epc_321_0),
    .cu_vector_31_0(control_unit_cu_vector_31_0), .cu_pc_src_2_0(control_unit_cu_pc_src_2_0),
    .idex_mem_r(idex_reg_idex_mem_r));
  idex_reg idex_reg (
    .idex_mem_w(idex_reg_idex_mem_w), .idex_mem_r(idex_reg_idex_mem_r), .clk(CLK),
    .idex_reg_w(idex_reg_idex_reg_w), .reset(RST), .idex_branch(idex_reg_idex_branch),
    .cu_stall(control_unit_cu_idex_stall), .idex_conition_2_0(idex_reg_idex_conition_2_0),
    .cu_flush(control_unit_cu_idex_flush), .idex_of_w_disen(idex_reg_idex_of_w_disen),
    .id_rd_addr_4_0(multiplexer_3_out), .idex_exres_sel(idex_reg_idex_exres_sel), .id_ctrl(decoder_id_ctrl),
    .idex_B_sel(idex_reg_idex_b_sel), .idex_ALU_op_3_0(idex_reg_idex_alu_op_3_0),
    .ifid_pc_31_0(ifid_reg_ifid_pc_31_0), .idex_shamt_sel(idex_reg_idex_shamt_sel),
    .idex_shift_op_1_0(idex_reg_idex_shift_op_1_0), .idex_shamt_4_0(idex_reg_idex_shamt_4_0),
    .ifid_pc_4_31_0(ifid_reg_ifid_pc_4_31_0), .idex_rs_addr_4_0(idex_reg_idex_rs_addr_4_0),
    .idex_rt_addr_4_0(idex_reg_idex_rt_addr_4_0), .idex_rd_addr_4_0(idex_reg_idex_rd_addr_4_0),
    .gpr_rs_31_0(GPR_rs_data_31_0), .idex_op_A_31_0(idex_reg_idex_op_a_31_0),
    .gpr_rt_31_0(multiplexer_2_out), .idex_op_B_31_0(idex_reg_idex_op_b_31_0),
    .id_imm_ext_31_0(\位扩展单元_imm_ext_31_0 ), .idex_imm_ext_31_0(idex_reg_idex_imm_ext_31_0),
    .idex_pc_31_0(idex_reg_idex_pc_31_0), .idex_pc_4_31_0(idex_reg_idex_pc_4_31_0),
    .idex_load_sel_2_0(idex_reg_idex_load_sel_2_0), .idex_store_sel_2_0(idex_reg_idex_store_sel_2_0),
    .idex_cp0_addr_4_0(idex_reg_idex_cp0_addr_4_0), .idex_syscall(idex_reg_idex_syscall),
    .idex_cp0_w_en(idex_reg_idex_cp0_w_en), .idex_eret(idex_reg_idex_eret), .idex_movz(idex_reg_idex_movz),
    .idex_movnz(idex_reg_idex_movnz));
  Multiplexer #(.select(2), .width(5), .enable("false")) multiplexer_3 (
    .in0(ifid_reg_ifid_rt_addr_4_0), .in1(ifid_reg_ifid_rd_addr_4_0), .in2(undriven_3),
    .out(multiplexer_3_out), .sel(decoder_id_rd_addr_sel_1_0));  // open: in3
  or or_1 (or_1_out, idex_reg_idex_movz, idex_reg_idex_movnz);
  forwarding_unit forwarding_unit_1 (
    .rs_data_31_0(idex_reg_idex_op_a_31_0), .rt_data_31_0(idex_reg_idex_op_b_31_0),
    .memwb_byte_en_3_0(memwb_reg_1_reg_byte_w_en_3_0_2), .rs_addr(idex_reg_idex_rs_addr_4_0),
    .rt_addr(idex_reg_idex_rt_addr_4_0), .memwb_rd_addr_4_0(memwb_reg_1_memwb_rd_addr_4_0),
    .input_A_31_0(forwarding_unit_1_input_a_31_0), .input_B_31_0(forwarding_unit_1_input_b_31_0),
    .A_sel_1_0(forwarding_unit_1_a_sel_1_0), .memwb_data_31_0(multiplexer_10_out),
    .B_sel_31_0(forwarding_unit_1_b_sel_31_0), .exmem_rd_addr(EXMEM_exmem_rd_addr_4_0),
    .exmem_byte_en_3_0(EXMEM_reg_byte_w_en_3_0_2));
  Multiplexer #(.select(2), .width(32), .enable("false")) multiplexer_4 (
    .in0(idex_reg_idex_op_a_31_0), .in1(EXMEM_exmem_alu_res_31_0), .in2(forwarding_unit_1_input_a_31_0),
    .out(multiplexer_4_out), .sel(forwarding_unit_1_a_sel_1_0));  // open: in3
  _32_5 u_32_5_1 (.in_1(multiplexer_4_out), .out_2(n32_5_1_out_2));
  Multiplexer #(.select(2), .width(32), .enable("false")) multiplexer_5 (
    .in0(idex_reg_idex_op_b_31_0), .in1(EXMEM_exmem_alu_res_31_0), .in2(forwarding_unit_1_input_b_31_0),
    .out(multiplexer_5_out), .sel(forwarding_unit_1_b_sel_31_0));  // open: in3
  Multiplexer #(.width(32), .enable("false")) multiplexer_6 (
    .in0(multiplexer_4_out), .in1(undriven_4), .out(multiplexer_6_out), .sel(or_1_out));
  Multiplexer #(.width(32), .enable("false")) multiplexer_7 (
    .in0(multiplexer_5_out), .in1(idex_reg_idex_imm_ext_31_0), .out(multiplexer_7_out),
    .sel(idex_reg_idex_b_sel));
  Multiplexer #(.width(5), .enable("false")) multiplexer_8 (
    .in0(idex_reg_idex_shamt_4_0), .in1(n32_5_1_out_2), .out(multiplexer_8_out), .sel(idex_reg_idex_shamt_sel));
  ALU alu_1 (
    .in_2(multiplexer_6_out), .in_3(multiplexer_7_out), .in_1(idex_reg_idex_alu_op_3_0), .out_4(alu_1_out_4),
    .out_5(alu_1_out_5), .out_6(alu_1_out_6), .out_7(alu_1_out_7));
  barrel_shifter barrel_shifter_1 (
    .shift_amount_4_0(multiplexer_8_out), .shift_op_1_0(idex_reg_idex_shift_op_1_0),
    .shift_in_31_0(multiplexer_5_out), .shift_out_31_0(barrel_shifter_1_shift_out_31_0));
  reg_w_gen reg_w_gen_1 (
    .in_3(idex_reg_idex_movz), .in_4(idex_reg_idex_movnz), .in_5(idex_reg_idex_reg_w),
    .in_6(idex_reg_idex_of_w_disen), .out_7(reg_w_gen_1_out_7), .in_1(alu_1_out_7), .in_2(alu_1_out_6));
  _32_2 u_32_2_1 (.in_1(alu_1_out_4), .out_2(n32_2_1_out_2));
  Adder #(.width(32)) adder_2 (
    .a(idex_reg_idex_imm_ext_31_0), .b(idex_reg_idex_pc_4_31_0), .out(adder_2_out));  // open: cin, cout
  lw_b_w_e_gen load_b_w_e_gen (
    .addr_1_0(n32_2_1_out_2), .load_sel_2_0(idex_reg_idex_load_sel_2_0),
    .b_w_en_3_0(load_b_w_e_gen_b_w_en_3_0));
  sw_b_w_e_gen store_b_w_e_gen (
    .addr_1_0(n32_2_1_out_2), .store_sel_2_0(idex_reg_idex_store_sel_2_0),
    .b_w_en_3_0(store_b_w_e_gen_b_w_en_3_0));
  real_rt_data_gen store_shifter (
    .addr_1_0(n32_2_1_out_2), .store_sel_2_0(idex_reg_idex_store_sel_2_0), .rt_data_31_0(multiplexer_5_out),
    .real_rt_data_31_0(store_shifter_real_rt_data_31_0));
  Multiplexer #(.select(2), .width(32), .enable("false")) multiplexer_9 (
    .in0(alu_1_out_4), .in1(barrel_shifter_1_shift_out_31_0), .in2(adder_2_out), .in3(multiplexer_4_out),
    .out(multiplexer_9_out), .sel(idex_reg_idex_exres_sel));
  exmem_reg EXMEM (
    .clk(CLK), .idex_branch(idex_reg_idex_branch), .reset(RST),
    .idex_condition_2_0(idex_reg_idex_conition_2_0), .cu_stall(control_unit_cu_exmem_stall),
    .cu_flush(control_unit_cu_exmem_flush), .adder_target_31_0(adder_2_out),
    .idex_mem_w(idex_reg_idex_mem_w), .idex_pc_31_0(idex_reg_idex_pc_31_0), .idex_memr(idex_reg_idex_mem_r),
    .idex_pc_4_31_0(idex_reg_idex_pc_4_31_0), .alu_lf(alu_1_out_5), .alu_zf(alu_1_out_6),
    .aligned_rt_data_31_0(store_shifter_real_rt_data_31_0), .ex_res_31_0(multiplexer_9_out),
    .real_rd_addr_4_0(idex_reg_idex_rd_addr_4_0), .idex_load_sel_2_0(idex_reg_idex_load_sel_2_0),
    .exmem_nen_w(EXMEM_exmem_nen_w), .exmem_mem_r(EXMEM_exmem_mem_r), .exmem_reg_w(EXMEM_exmem_reg_w),
    .exmem_condition_2_0(EXMEM_exmem_condition_2_0), .exmem_branch(EXMEM_exmem_branch),
    .exmem_alu_res_31_0(EXMEM_exmem_alu_res_31_0), .exmem_rt_data_31_0(EXMEM_exmem_rt_data_31_0),
    .exmem_target_31_0(EXMEM_exmem_target_31_0), .exmem_lf(EXMEM_exmem_lf), .exmem_zf(EXMEM_exmem_zf),
    .exmem_pc_31_0(EXMEM_exmem_pc_31_0), .exmem_pc_4_31_0(EXMEM_exmem_pc_4_31_0),
    .exmem_rd_addr_4_0(EXMEM_exmem_rd_addr_4_0), .exmem_load_sel_2_0(EXMEM_exmem_load_sel_2_0),
    .reg_byte_w_en_3_0(load_b_w_e_gen_b_w_en_3_0), .mem_byte_w_en_3_0(store_b_w_e_gen_b_w_en_3_0),
    .reg_byte_w_en_3_0_2(EXMEM_reg_byte_w_en_3_0_2), .mem_byte_w_en(EXMEM_mem_byte_w_en),
    .idex_cp0_dst_addr_4_0(idex_reg_idex_cp0_addr_4_0), .cp0_w_en(idex_reg_idex_cp0_w_en),
    .syscall(idex_reg_idex_syscall), .exmem_cp0_dst_addr_4_0(EXMEM_exmem_cp0_dst_addr_4_0),
    .cp0_w_en_2(EXMEM_cp0_w_en_2), .syscall_2(EXMEM_syscall_2), .idex_eret(idex_reg_idex_eret),
    .exmem_eret(EXMEM_exmem_eret), .alu_of(alu_1_out_7), .idex_reg_w(reg_w_gen_1_out_7));  // open: exmem_store_sel_2_0
  cp0 cp0_1 (
    .cu_cp0_w_en(control_unit_cu_cp0_w_en), .cu_exec_code_4_0(control_unit_cu_exec_code_4_0),
    .wb_cp0_w_en(memwb_reg_1_memwb_cp0_w_en), .wb_cp0_data_in_31_0(memwb_reg_1_aligned_rt_data_31_0_2),
    .eoc_31_0(control_unit_cu_epc_321_0), .cp0_data_31_0(cp0_1_cp0_data_31_0), .cp0_intr(cp0_1_cp0_intr),
    .cp0_epc_31_0(cp0_1_cp0_epc_31_0), .interruption_7_0(INTERRUPTIONS),
    .id_cp0_src_addr_4_0(decoder_cp0_src_addr_3_0), .wb_cp0_dst_addr_4_0(memwb_reg_1_memwb_cp0_dst_addr_4_0));
  final_target final_target_1 (
    .exmem_branch(EXMEM_exmem_branch), .exmem_condition_2_0(EXMEM_exmem_condition_2_0),
    .exmem_lf(EXMEM_exmem_lf), .exmem_zf(EXMEM_exmem_zf), .exmem_target_31_0(EXMEM_exmem_target_31_0),
    .exmem_pc_4_31_0(EXMEM_exmem_pc_4_31_0), .final_target_31_0(final_target_1_final_target_31_0));
  data_mem_interface data_mem_interface (
    .read(EXMEM_exmem_mem_r), .write(EXMEM_exmem_nen_w), .addr_31_0(EXMEM_exmem_alu_res_31_0),
    .data_in_31_0(EXMEM_exmem_rt_data_31_0), .data_out_31_0(data_mem_interface_data_out_31_0),
    .mem_stall(instr_mem_interface_men_stall), .clk(CLK), .mem_byte_w_en(EXMEM_mem_byte_w_en), .reset(RST));
  _32_2 u_32_2_2 (.in_1(EXMEM_exmem_alu_res_31_0), .out_2(n32_2_2_out_2));
  mem_r_data_shift load_shifter (
    .in_1(n32_2_2_out_2), .in_2(EXMEM_exmem_load_sel_2_0), .in_3(data_mem_interface_data_out_31_0),
    .out_4(load_shifter_out_4));
  memwb_reg memwb_reg_1 (
    .clk(CLK), .reset(RST), .exmem_mem_r(EXMEM_exmem_mem_r), .exmem_mem_w(EXMEM_exmem_reg_w),
    .exmem_rd_addr_4_0(EXMEM_exmem_rd_addr_4_0), .reg_byte_w_en_3_0(EXMEM_reg_byte_w_en_3_0_2),
    .mem_data_31_0(load_shifter_out_4), .ex_data_31_0(EXMEM_exmem_alu_res_31_0),
    .memwb_mem_r(memwb_reg_1_memwb_mem_r), .memwb_reg_w(memwb_reg_1_memwb_reg_w),
    .memwb_rd_addr_4_0(memwb_reg_1_memwb_rd_addr_4_0), .reg_byte_w_en_3_0_2(memwb_reg_1_reg_byte_w_en_3_0_2),
    .memwb_memdata_31_0(memwb_reg_1_memwb_memdata_31_0), .memwb_exdata_31_0(memwb_reg_1_memwb_exdata_31_0),
    .exmem_cp0_dst_addr_4_0(EXMEM_exmem_cp0_dst_addr_4_0), .exmem_cp0_w_en(EXMEM_cp0_w_en_2),
    .memwb_cp0_dst_addr_4_0(memwb_reg_1_memwb_cp0_dst_addr_4_0), .memwb_cp0_w_en(memwb_reg_1_memwb_cp0_w_en),
    .aligned_rt_data_31_0(EXMEM_exmem_rt_data_31_0),
    .aligned_rt_data_31_0_2(memwb_reg_1_aligned_rt_data_31_0_2));
  Multiplexer #(.width(32), .enable("false")) multiplexer_10 (
    .in0(memwb_reg_1_memwb_memdata_31_0), .in1(memwb_reg_1_memwb_exdata_31_0), .out(multiplexer_10_out),
    .sel(memwb_reg_1_memwb_mem_r));

  // Notes on the sheet:
  //   4
  //   5'b0000
  //   JR使用的从Rs读出的数据
  //   byte_en
  //   addr
  //   write
  //   data
  //   5'b11111
  //   Rd_addr_sel
  //   new_reg_w = ((movnz && zf) || (movz && !zf) || (id_of_w_disen && of)) ? 0 : idex_reg_w
  //   32'd0
  //   Rt_imm_sel
  //   shift_amount_sel
  //   ALU
  //   Barrel Shifter
  //   calculate_branch_addr
  //   Exec_res_sel
endmodule

module ifid_reg (
  input  clk,
  input  reset,
  input  cu_stall,
  input  cu_flush,
  input  [31:0] pc_31_0,
  input  [31:0] pc_4_31_0,
  input  [31:0] instr_31_0,
  output [31:0] ifid_pc_31_0,
  output [31:0] ifid_pc_4_31_0,
  output [31:0] ifid_jump_instr_31_0,
  output [31:0] ifid_instr_31_0,
  output [4:0] ifid_rs_addr_4_0,
  output [4:0] ifid_rt_addr_4_0,
  output [15:0] ifid_imm_15_0,
  output [4:0] ifid_rd_addr_4_0
);
endmodule

module decoder (
  input  [31:0] ifid_instr_31_0,
  output [4:0] cp0_src_addr_3_0,
  output id_rt_data_sel,
  output [1:0] id_rd_addr_sel_1_0,
  output id_in,
  output id_jump,
  output id_ctrl,
  output [1:0] in_imm_ext_1_0,
  output id_rt_addr_sel
);
endmodule

module idex_reg (
  input  clk,
  input  reset,
  input  cu_stall,
  input  cu_flush,
  input  [4:0] id_rd_addr_4_0,
  input  id_ctrl,
  input  [31:0] ifid_pc_31_0,
  input  [31:0] ifid_pc_4_31_0,
  input  [31:0] gpr_rs_31_0,
  input  [31:0] gpr_rt_31_0,
  input  [31:0] id_imm_ext_31_0,
  output idex_movz,
  output idex_movnz,
  output idex_mem_w,
  output idex_mem_r,
  output idex_reg_w,
  output idex_branch,
  output [2:0] idex_conition_2_0,
  output idex_of_w_disen,
  output [1:0] idex_exres_sel,
  output idex_B_sel,
  output [3:0] idex_ALU_op_3_0,
  output idex_shamt_sel,
  output [4:0] idex_shamt_4_0,
  output [1:0] idex_shift_op_1_0,
  output [31:0] idex_imm_ext_31_0,
  output [4:0] idex_rd_addr_4_0,
  output [31:0] idex_pc_31_0,
  output [31:0] idex_pc_4_31_0,
  output [2:0] idex_load_sel_2_0,
  output [2:0] idex_store_sel_2_0,
  output [31:0] idex_op_A_31_0,
  output [31:0] idex_op_B_31_0,
  output [4:0] idex_rs_addr_4_0,
  output [4:0] idex_rt_addr_4_0,
  output [4:0] idex_cp0_addr_4_0,
  output idex_cp0_w_en,
  output idex_syscall,
  output idex_eret
);
endmodule

module exmem_reg (
  input  clk,
  input  reset,
  input  cu_stall,
  input  cu_flush,
  input  idex_mem_w,
  input  idex_memr,
  input  idex_reg_w,
  input  idex_branch,
  input  [2:0] idex_condition_2_0,
  input  [31:0] adder_target_31_0,
  input  alu_lf,
  input  alu_zf,
  input  alu_of,
  input  [31:0] ex_res_31_0,
  input  [4:0] real_rd_addr_4_0,
  input  [2:0] idex_load_sel_2_0,
  input  [3:0] reg_byte_w_en_3_0,
  input  [3:0] mem_byte_w_en_3_0,
  input  [31:0] idex_pc_31_0,
  input  [31:0] idex_pc_4_31_0,
  input  [31:0] aligned_rt_data_31_0,
  input  [4:0] idex_cp0_dst_addr_4_0,
  input  cp0_w_en,
  input  syscall,
  input  idex_eret,
  output [31:0] exmem_pc_31_0,
  output exmem_nen_w,
  output exmem_mem_r,
  output exmem_reg_w,
  output [3:0] reg_byte_w_en_3_0_2,
  output [4:0] exmem_rd_addr_4_0,
  output [3:0] mem_byte_w_en,
  output [31:0] exmem_alu_res_31_0,
  output [31:0] exmem_rt_data_31_0,
  output exmem_branch,
  output [2:0] exmem_condition_2_0,
  output [31:0] exmem_target_31_0,
  output [31:0] exmem_pc_4_31_0,
  output exmem_lf,
  output exmem_zf,
  output [2:0] exmem_load_sel_2_0,
  output [2:0] exmem_store_sel_2_0,
  output [4:0] exmem_cp0_dst_addr_4_0,
  output cp0_w_en_2,
  output syscall_2,
  output exmem_eret
);
endmodule

module memwb_reg (
  input  clk,
  input  reset,
  input  exmem_mem_r,
  input  exmem_mem_w,
  input  [3:0] reg_byte_w_en_3_0,
  input  [4:0] exmem_rd_addr_4_0,
  input  [31:0] mem_data_31_0,
  input  [31:0] ex_data_31_0,
  input  [4:0] exmem_cp0_dst_addr_4_0,
  input  exmem_cp0_w_en,
  input  [31:0] aligned_rt_data_31_0,
  output memwb_mem_r,
  output memwb_reg_w,
  output [4:0] memwb_rd_addr_4_0,
  output [3:0] reg_byte_w_en_3_0_2,
  output [31:0] memwb_memdata_31_0,
  output [31:0] memwb_exdata_31_0,
  output [4:0] memwb_cp0_dst_addr_4_0,
  output memwb_cp0_w_en,
  output [31:0] aligned_rt_data_31_0_2
);
endmodule

module ALU (
  input  [3:0] in_1,
  input  [31:0] in_2,
  input  [31:0] in_3,
  output [31:0] out_4,
  output out_5,
  output out_6,
  output out_7
);
endmodule

module lw_b_w_e_gen (
  input  [1:0] addr_1_0,
  input  [2:0] load_sel_2_0,
  output [3:0] b_w_en_3_0
);
endmodule

module sw_b_w_e_gen (
  input  [1:0] addr_1_0,
  input  [2:0] store_sel_2_0,
  output [3:0] b_w_en_3_0
);
endmodule

module real_rt_data_gen (
  input  [1:0] addr_1_0,
  input  [2:0] store_sel_2_0,
  input  [31:0] rt_data_31_0,
  output [31:0] real_rt_data_31_0
);
endmodule

module barrel_shifter (
  input  [4:0] shift_amount_4_0,
  input  [1:0] shift_op_1_0,
  input  [31:0] shift_in_31_0,
  output [31:0] shift_out_31_0
);
endmodule

// rt_sel
module rt_data_sel (
  input  [31:0] in_1,
  output [31:0] out_2
);
endmodule

// rs_sel
module rs_data_sel (
  input  [31:0] in_1,
  output [31:0] out_2
);
endmodule

module _32_2 (
  input  [31:0] in_1,
  output [1:0] out_2
);
endmodule

module _32_5 (
  input  [31:0] in_1,
  output [4:0] out_2
);
endmodule

module GPR (
  input  clk,
  input  reset,
  input  [4:0] Rs_addr_4_0,
  input  [4:0] Rt_addr_4_0,
  input  [31:0] data_in_31_0,
  input  write,
  input  [4:0] Rd_addr_4_0,
  input  [3:0] Rd_byte_w_en_3_0,
  output [31:0] Rs_data_31_0,
  output [31:0] Rt_data_31_0
);
endmodule

module data_mem_interface (
  input  clk,
  input  reset,
  input  read,
  input  write,
  input  [31:0] addr_31_0,
  input  [31:0] data_in_31_0,
  input  [3:0] mem_byte_w_en,
  output [31:0] data_out_31_0,
  output mem_stall
);
endmodule

module mem_r_data_shift (
  input  [1:0] in_1,
  input  [2:0] in_2,
  input  [31:0] in_3,
  output [31:0] out_4
);
endmodule

module final_target (
  input  exmem_branch,
  input  [2:0] exmem_condition_2_0,
  input  [31:0] exmem_target_31_0,
  input  [31:0] exmem_pc_4_31_0,
  input  exmem_lf,
  input  exmem_zf,
  output [31:0] final_target_31_0
);
endmodule

module instr_mem_interface (
  input  clk,
  input  cache_flush,
  input  [31:0] addr_31_0,
  output [31:0] instr_31_0,
  output men_stall
);
endmodule

module pc (
  input  stall,
  input  clk,
  input  reset,
  input  [31:0] pc_in_31_0,
  output [31:0] pc_out_31_0
);
endmodule

module imm_ext (
  input  [15:0] ifid_imm_15_0,
  input  [1:0] id_imm_ext_1_0,
  output [31:0] imm_ext_31_0
);
endmodule

module control_unit (
  input  id_jr,
  input  mem_stall,
  input  id_jmp,
  input  exmem_syscall,
  input  idex_mem_r,
  input  [4:0] real_rs_addr_4_0,
  input  [4:0] real_rt_addr_4_0,
  input  [4:0] real_rd_addr_4_0,
  input  [31:0] preedicted_idex_pc_31_0,
  input  [31:0] target_exmem_pc_31_0,
  input  cp0_intr,
  input  exmem_eret,
  output [2:0] cu_pc_src_2_0,
  output cu_pc_stall,
  output cu_ifid_stall,
  output cu_ifid_flush,
  output cu_idex_stall,
  output cu_idex_flush,
  output cu_exmem_stall,
  output cu_exmem_flush,
  output bpu_write_en,
  output cu_cp0_w_en,
  output [4:0] cu_exec_code_4_0,
  output [31:0] cu_epc_321_0,
  output [31:0] cu_vector_31_0
);
endmodule

module forwarding_unit (
  input  [31:0] rs_data_31_0,
  input  [31:0] rt_data_31_0,
  input  [4:0] rs_addr,
  input  [4:0] rt_addr,
  input  [3:0] exmem_byte_en_3_0,
  input  [4:0] exmem_rd_addr,
  input  [3:0] memwb_byte_en_3_0,
  input  [4:0] memwb_rd_addr_4_0,
  input  [31:0] memwb_data_31_0,
  output [31:0] input_A_31_0,
  output [31:0] input_B_31_0,
  output [1:0] A_sel_1_0,
  output [1:0] B_sel_31_0
);
endmodule

module branch_predict_unit (
  input  [31:0] current_pc_31_0,
  input  [31:0] tag_pc_31_0,
  input  [31:0] next_pc_31_0,
  input  bpu_write_en,
  output [31:0] predicted_pc_31_0
);
endmodule

module cp0 (
  input  cu_cp0_w_en,
  input  [4:0] cu_exec_code_4_0,
  input  [7:0] interruption_7_0,
  input  [4:0] id_cp0_src_addr_4_0,
  input  wb_cp0_w_en,
  input  [4:0] wb_cp0_dst_addr_4_0,
  input  [31:0] wb_cp0_data_in_31_0,
  input  [31:0] eoc_31_0,
  output [31:0] cp0_data_31_0,
  output cp0_intr,
  output [31:0] cp0_epc_31_0
);
endmodule

module exception (
  input  in_1,
  input  [31:0] in_2,
  output out_3,
  output [4:0] out_4
);
endmodule

module pc_src_selector (
  input  [2:0] PC_SRC_2_0,
  input  [31:0] J_31_0,
  input  [31:0] JR_31_0,
  input  [31:0] VECTOR_31_0,
  input  [31:0] EPC_31_0,
  input  [31:0] TARGET_31_0,
  input  [31:0] BPU_31_0,
  output [31:0] PC_31_0
);
endmodule

module reg_w_gen (
  input  in_1,
  input  in_2,
  input  in_3,
  input  in_4,
  input  in_5,
  input  in_6,
  output out_7
);
endmodule
